// Logisim project cache.circ as structural Verilog: 1 circuit, main circuit cache
module cache (
  input  [13:0] CPU_Address,
  input  [31:0] code,
  input  CLOCK,
  input  RESET,
  output HIT
);

  wire and_5_out, and_6_out, and_7_out, and_8_out, and_9_out, and_10_out, and_11_out, and_12_out, clock1,
       clock2, clock4, comparator_1_eq, comparator_2_eq, comparator_3_eq, comparator_4_eq, comparator_5_eq,
       comparator_6_eq, comparator_7_eq, comparator_8_eq, decoder_2_out0, decoder_2_out1, decoder_3_out0,
       decoder_3_out1, decoder_4_out0, decoder_4_out1, decoder_5_out0, decoder_5_out1, hit1, hit2, hit3,
       hit4, LRU1, LRU2, LRU3, LRU4, not_1_out, not_2_out, not_3_out, not_4_out, set1, set2, set3, set4, v11,
       v12, v21, v22, v31, v32, v41, v42;
  wire [9:0] register_13_q, register_14_q, register_15_q, register_16_q, register_17_q, register_18_q,
       register_19_q, register_20_q;

  and and_1 (clock1, CLOCK, set1);
  Register #(.width(1)) register_1 (.en(1'b1), .clk(clock4), .Q(LRU4), .clr(RESET));  // open: D
  Register #(.width(1)) register_2 (.en(1'b1), .clk(clock2), .Q(LRU1), .clr(RESET));  // open: D
  Register #(.width(1)) register_3 (.en(1'b1), .clk(clock2), .Q(LRU2), .clr(RESET));  // open: D
  Register #(.width(1)) register_4 (.en(1'b1), .clk(RESET), .Q(LRU3), .clr(RESET));  // open: D
  Register #(.width(1)) register_5 (.en(1'b1), .clk(clock2), .Q(v11), .clr(RESET));  // open: D
  Register #(.width(1)) register_6 (.en(1'b1), .clk(clock2), .Q(v12), .clr(RESET));  // open: D
  Register #(.width(1)) register_7 (.en(1'b1), .clk(clock2), .Q(v21), .clr(RESET));  // open: D
  Register #(.width(1)) register_8 (.en(1'b1), .clk(clock2), .Q(v22), .clr(RESET));  // open: D
  Register #(.width(1)) register_9 (.en(1'b1), .clk(RESET), .Q(v31), .clr(RESET));  // open: D
  Register #(.width(1)) register_10 (.en(1'b1), .clk(RESET), .Q(v32), .clr(RESET));  // open: D
  Register #(.width(1)) register_11 (.en(1'b1), .clk(clock4), .Q(v41), .clr(RESET));  // open: D
  Register #(.width(1)) register_12 (.en(1'b1), .clk(clock4), .Q(v42), .clr(RESET));  // open: D
  and and_2 (clock2, CLOCK, set2);
  Decoder #(.select(2)) decoder_1 (
    .out0(set1), .out1(set2), .out2(set3), .out3(set4), .sel(CPU_Address[11:10]), .en(1'b1));
  Register #(.width(10)) register_13 (.en(1'b1), .clk(clock2), .Q(register_13_q), .clr(RESET));  // open: D
  Register #(.width(10)) register_14 (.en(1'b1), .clk(clock2), .Q(register_14_q), .clr(RESET));  // open: D
  Register #(.width(10)) register_15 (.en(1'b1), .clk(clock2), .Q(register_15_q), .clr(RESET));  // open: D
  Register #(.width(10)) register_16 (.en(1'b1), .clk(clock2), .Q(register_16_q), .clr(RESET));  // open: D
  Register #(.width(10)) register_17 (.en(1'b1), .clk(RESET), .Q(register_17_q), .clr(RESET));  // open: D
  Register #(.width(10)) register_18 (.en(1'b1), .clk(RESET), .Q(register_18_q), .clr(RESET));  // open: D
  Register #(.width(10)) register_19 (.en(1'b1), .clk(clock4), .Q(register_19_q), .clr(RESET));  // open: D
  Register #(.width(10)) register_20 (.en(1'b1), .clk(clock4), .Q(register_20_q), .clr(RESET));  // open: D
  and and_3 (RESET, CLOCK, set3);
  set u_set1 (.RESET(RESET));  // open: data_in, word_index, block_index, CLOCK
  set u_set2 (.RESET(RESET));  // open: data_in, word_index, block_index, CLOCK
  set u_set3 (.RESET(RESET));  // open: data_in, word_index, block_index, CLOCK
  set u_set4 (.RESET(RESET));  // open: data_in, word_index, block_index, CLOCK
  Comparator #(.mode("unsigned"), .width(10)) comparator_1 (
    .a(register_13_q), .b(CPU_Address[9:0]), .eq(comparator_1_eq));  // open: gt, lt
  Comparator #(.mode("unsigned"), .width(10)) comparator_2 (
    .a(register_14_q), .b(CPU_Address[9:0]), .eq(comparator_2_eq));  // open: gt, lt
  Comparator #(.mode("unsigned"), .width(10)) comparator_3 (
    .a(register_15_q), .b(CPU_Address[9:0]), .eq(comparator_3_eq));  // open: gt, lt
  Comparator #(.mode("unsigned"), .width(10)) comparator_4 (
    .a(register_16_q), .b(CPU_Address[9:0]), .eq(comparator_4_eq));  // open: gt, lt
  Comparator #(.mode("unsigned"), .width(10)) comparator_5 (
    .a(register_17_q), .b(CPU_Address[9:0]), .eq(comparator_5_eq));  // open: gt, lt
  Comparator #(.mode("unsigned"), .width(10)) comparator_6 (
    .a(register_18_q), .b(CPU_Address[9:0]), .eq(comparator_6_eq));  // open: gt, lt
  Comparator #(.mode("unsigned"), .width(10)) comparator_7 (
    .a(register_19_q), .b(CPU_Address[9:0]), .eq(comparator_7_eq));  // open: gt, lt
  Comparator #(.mode("unsigned"), .width(10)) comparator_8 (
    .a(register_20_q), .b(CPU_Address[9:0]), .eq(comparator_8_eq));  // open: gt, lt
  and and_4 (clock4, CLOCK, set4);
  and and_5 (and_5_out, v11, comparator_1_eq);
  and and_6 (and_6_out, v12, comparator_2_eq);
  and and_7 (and_7_out, v21, comparator_3_eq);
  and and_8 (and_8_out, v22, comparator_4_eq);
  and and_9 (and_9_out, v31, comparator_5_eq);
  and and_10 (and_10_out, v32, comparator_6_eq);
  and and_11 (and_11_out, v41, comparator_7_eq);
  and and_12 (and_12_out, v42, comparator_8_eq);
  Decoder decoder_2 (.out0(decoder_2_out0), .out1(decoder_2_out1), .sel(LRU1), .en(not_1_out));
  not not_1 (not_1_out, hit1);
  or or_1 (hit1, and_5_out, and_6_out);
  Decoder decoder_3 (.out0(decoder_3_out0), .out1(decoder_3_out1), .sel(LRU2), .en(not_2_out));
  not not_2 (not_2_out, hit2);
  or or_2 (hit2, and_7_out, and_8_out);
  Decoder decoder_4 (.out0(decoder_4_out0), .out1(decoder_4_out1), .sel(LRU3), .en(not_3_out));
  not not_3 (not_3_out, hit3);
  or or_3 (hit3, and_9_out, and_10_out);
  Decoder decoder_5 (.out0(decoder_5_out0), .out1(decoder_5_out1), .sel(LRU4), .en(not_4_out));
  not not_4 (not_4_out, hit4);
  or or_4 (hit4, and_11_out, and_12_out);
  Register #(.width(1)) register_21 (.D(decoder_2_out0), .en(1'b1), .clk(clock1), .clr(RESET));  // open: Q
  Register #(.width(1)) register_22 (.D(decoder_2_out1), .en(1'b1), .clk(clock1), .clr(RESET));  // open: Q
  Register #(.width(1)) register_23 (.D(decoder_3_out0), .en(1'b1), .clk(clock2), .clr(RESET));  // open: Q
  Register #(.width(1)) register_24 (.D(decoder_3_out1), .en(1'b1), .clk(clock2), .clr(RESET));  // open: Q
  Register #(.width(1)) register_25 (.D(decoder_4_out0), .en(1'b1), .clk(RESET), .clr(RESET));  // open: Q
  Register #(.width(1)) register_26 (.D(decoder_4_out1), .en(1'b1), .clk(RESET), .clr(RESET));  // open: Q
  Register #(.width(1)) register_27 (.D(decoder_5_out0), .en(1'b1), .clk(clock4), .clr(RESET));  // open: Q
  Register #(.width(1)) register_28 (.D(decoder_5_out1), .en(1'b1), .clk(clock4), .clr(RESET));  // open: Q
  or or_5 (HIT, hit1, hit2, hit3, hit4);

  // Other names for the same wires on the sheet: clock3 = RESET; tag[9:0] = CPU_Address[9:0];
  //   set_index[1:0] = CPU_Address[11:10]; word_index[1:0] = CPU_Address[13:12]

  // Notes on the sheet:
  //   tag: 10 bit, set: 2bit, word: 2bit
  //   if 0: block1 else: block 2
  //   LRU bit
  //   LRU bit
  //   LRU bit
  //   LRU bit
  //   valid bit
  //   valid bit
  //   valid bit
  //   valid bit
  //   tag array
  //   tag array
  //   tag array
  //   tag array
  //   works: dirty bit/ tag bits/ transfering beetwin m.m and c.m and cpu / LRU
  //   dirty bit
  //   dirty bit
endmodule
