// Logisim project cpu.circ as structural Verilog: 1 circuit, main circuit cpu
module cpu (
  input  in_1
);

  wire alu_1_zero, ALU_v, ALUSrc, ALUSrc_out, ALUv_out, and_1_out, Branch, BranchOut, clk, clk_main, Hit,
       JAL, Jump, Jump_out, LRU_OUT, LRU_TMP, MemToReg, MemToReg_out, not_1_out, not_2_out, RegDst,
       RegDst_out, RegWrite, RegWrite_out, syscall, syscall_out;
  wire [3:0] MemWriteMask, MemWriteMask_out, writeMask_cache;
  wire [4:0] multiplexer_2_out, rd, rd_out, rs, rs_out, rt, rt_out, shamt, shamt_out, writeInd;
  wire [5:0] ALU_op, ALUop_out, func, funcOut, opcode, opcode_out;
  wire [15:0] imm16, immOut;
  wire [25:0] target26, target26_out;
  wire [27:0] sxl2_1_t28;
  wire [31:0] adder_2_out, ALUResult, ALUResult_out, BResult, BResult_out, cacheOut, immIN, immINout, in1,
       in1_out, in2, in2_out, JCU_OUT, Jcu_outF, memdelayed_1_memreaddata, multiplexer_6_out, outMM,
       programcounter_1_pc_out, RD1, RD1_out, RD2, RD2_out, shifter_1_out, writeback, writeback_out, writeDat;

  not not_1 (not_1_out, syscall_out);
  Adder #(.width(32)) adder_1 (.a(programcounter_1_pc_out), .b(32'h4), .out(in2));  // open: cin, cout
  ProgramCounter programcounter_1 (.PC_in(JCU_OUT), .En(not_1_out), .CLK(clk), .PC_out(programcounter_1_pc_out));
  Multiplexer #(.width(32)) multiplexer_1 (
    .in0(BResult_out), .in1({in2[31:28], sxl2_1_t28}), .out(in1), .sel(Jump_out));
  SXL2 sxl2_1 (.T26(target26), .T28(sxl2_1_t28));
  memDelayed memdelayed_1 (
    .MemAddress(programcounter_1_pc_out), .clk(clk), .MemReadData(memdelayed_1_memreaddata));  // open: MemWriteMask, MemWriteData
  instruction_splitter instruction_splitter_1 (
    .instruction(memdelayed_1_memreaddata), .op(opcode), .target26(target26), .rs(rs), .rt(rt),
    .imm16(imm16), .rd(rd), .shamt(shamt), .func(func));
  Register #(.width(32)) register_1 (.D(in2), .en(1'b1), .clk(clk), .Q(in2_out), .clr(in_1));
  Register #(.width(32)) register_2 (.D(in1), .en(1'b1), .clk(clk), .Q(in1_out), .clr(in_1));
  Register #(.width(6)) register_3 (.D(opcode), .en(1'b1), .clk(clk), .Q(opcode_out), .clr(in_1));
  Register #(.width(26)) register_4 (.D(target26), .en(1'b1), .clk(clk), .Q(target26_out), .clr(in_1));
  Register #(.width(5)) register_5 (.D(rs), .en(1'b1), .clk(clk), .Q(rs_out), .clr(in_1));
  Register #(.width(5)) register_6 (.D(rt), .en(1'b1), .clk(clk), .Q(rt_out), .clr(in_1));
  Register #(.width(16)) register_7 (.D(imm16), .en(1'b1), .clk(clk), .Q(immOut), .clr(in_1));
  Register #(.width(5)) register_8 (.D(rd), .en(1'b1), .Q(rd_out), .clr(in_1));  // open: clk
  Register #(.width(5)) register_9 (.D(shamt), .en(1'b1), .clk(clk), .Q(shamt_out), .clr(in_1));
  Register #(.width(6)) register_10 (.D(func), .en(1'b1), .clk(clk), .Q(funcOut), .clr(in_1));
  Multiplexer #(.width(5)) multiplexer_2 (.in0(rt_out), .in1(rd_out), .out(multiplexer_2_out), .sel(RegDst));
  Multiplexer #(.width(32)) multiplexer_3 (.in0(writeback_out), .in1(JCU_OUT), .out(writeDat), .sel(JAL));
  Multiplexer #(.width(5)) multiplexer_4 (.in0(multiplexer_2_out), .in1({5{1'b1}}), .out(writeInd), .sel(JAL));
  JCU jcu_1 (.Func(funcOut), .in1(in1_out), .rs(rs_out), .Y(JCU_OUT));
  CU cu_1 (
    .Func(funcOut), .Opcode(opcode_out), .JAL(JAL), .ALUSrc(ALUSrc), .ALUop(ALU_op), .syscall(syscall),
    .RegDst(RegDst), .ALU_V(ALU_v), .MemToReg(MemToReg), .RegWrite(RegWrite), .MemWriteMask(MemWriteMask),
    .Branch(Branch), .Jump(Jump));
  SignExtend signextend_1 (.S16(immOut), .S32(immIN));
  regfile regfile_1 (
    .ReadIndex1(rs_out), .ReadIndex2(rt_out), .WriteIndex(writeInd), .WriteData(writeDat), .RegWEn(RegWrite),
    .clk(clk), .ReadData1(RD1), .ReadData2(RD2));
  Register #(.width(32)) register_11 (.D(immIN), .en(1'b1), .clk(clk), .Q(immINout), .clr(in_1));
  Register #(.width(32)) register_12 (.D(JCU_OUT), .en(1'b1), .clk(clk), .Q(Jcu_outF), .clr(in_1));
  Register #(.width(1)) register_13 (.D(ALUSrc), .en(1'b1), .clk(clk), .Q(ALUSrc_out), .clr(in_1));
  Register #(.width(6)) register_14 (.D(ALU_op), .en(1'b1), .clk(clk), .Q(ALUop_out), .clr(in_1));
  Register #(.width(1)) register_15 (.D(RegDst), .en(1'b1), .clk(clk), .Q(RegDst_out), .clr(in_1));
  Register #(.width(1)) register_16 (.D(ALU_v), .en(1'b1), .clk(clk), .Q(ALUv_out), .clr(in_1));
  Register #(.width(1)) register_17 (.D(MemToReg), .en(1'b1), .clk(clk), .Q(MemToReg_out), .clr(in_1));
  Register #(.width(1)) register_18 (.D(RegWrite), .en(1'b1), .clk(clk), .Q(RegWrite_out), .clr(in_1));
  Register #(.width(4)) register_19 (.D(MemWriteMask), .en(1'b1), .clk(clk), .Q(MemWriteMask_out), .clr(in_1));
  Register #(.width(1)) register_20 (.D(Branch), .en(1'b1), .clk(clk), .Q(BranchOut), .clr(in_1));
  Register #(.width(1)) register_21 (.D(Jump), .en(1'b1), .clk(clk), .Q(Jump_out), .clr(in_1));
  Register #(.width(32)) register_22 (.D(RD1), .en(1'b1), .clk(clk), .Q(RD1_out), .clr(in_1));
  Register #(.width(32)) register_23 (.D(RD2), .en(1'b1), .clk(clk), .Q(RD2_out), .clr(in_1));
  Register #(.width(1)) register_24 (.D(syscall), .en(1'b1), .clk(clk), .Q(syscall_out), .clr(in_1));
  Shifter #(.width(32)) shifter_1 (.in(immINout), .\dist (5'b00010), .out(shifter_1_out));
  Adder #(.width(32)) adder_2 (.a(in2_out), .b(shifter_1_out), .out(adder_2_out));  // open: cin, cout
  Multiplexer #(.width(32)) multiplexer_5 (.in0(in2_out), .in1(adder_2_out), .out(BResult), .sel(and_1_out));
  and and_1 (and_1_out, BranchOut, alu_1_zero);
  ALU alu_1 (
    .A(RD1_out), .B(RD2_out), .ALUOp(ALUop_out), .Func(funcOut), .Imm(immINout), .Shamt(shamt_out),
    .ALUSrc(ALUSrc_out), .Zero(alu_1_zero), .ALUResult(ALUResult));
  Register #(.width(32)) register_25 (.D(BResult), .en(1'b1), .clk(clk), .Q(BResult_out), .clr(in_1));
  Register #(.width(32)) register_26 (.D(ALUResult), .en(1'b1), .clk(clk), .Q(ALUResult_out), .clr(in_1));
  Clock clock_1 (.out(clk_main));
  not not_2 (not_2_out, clk);
  Multiplexer #(.width(32)) multiplexer_6 (.in0(outMM), .in1(RD2_out), .out(multiplexer_6_out), .sel(Hit));
  memDelayed memdelayed_2 (
    .MemAddress(ALUResult_out), .MemWriteMask(writeMask_cache), .MemWriteData(RD2_out), .clk(not_2_out),
    .MemReadData(outMM));
  cahceCU cahcecu_1 (.CPU_Address(ALUResult_out), .LRU(LRU_OUT), .CLOCK(clk), .RESET(in_1), .LRU_out(LRU_TMP));
  cache cache_1 (
    .CPU_Address(ALUResult_out), .memWriteData(multiplexer_6_out), .MemWriteMask(MemWriteMask_out),
    .LRU(LRU_TMP), .clock(clk_main), .reset(in_1), .raedData(cacheOut), .Hit(Hit), .LRU_out(LRU_OUT),
    .writeMask(writeMask_cache));
  Multiplexer multiplexer_7 (.in0(1'b0), .in1(clk_main), .out(clk), .sel(Hit));
  Multiplexer #(.width(32)) multiplexer_8 (.in0(ALUResult_out), .in1(cacheOut), .out(writeback), .sel(MemToReg_out));
  Register #(.width(32)) register_27 (.D(writeback), .en(1'b1), .clk(clk), .Q(writeback_out), .clr(in_1));

  // Other names for the same wires on the sheet: reset = in_1

  // Notes on the sheet:
  //   IF/ID
  //   ID/EXE
  //   EXE/MEM
  //   MEM/WB
endmodule
